// Logisim project 实验三_2.circ as structural Verilog: 2 circuits, main circuit main
module main (
  input  CLR_L,
  output out_2,
  output out_3,
  output out_4,
  output out_5,
  output out_6
);

  wire clock_1_out, clock_2_out, d_ff_1_qn, d_ff_2_qn, d_ff_3_qn, d_ff_4_qn, d_ff_5_qn, nand_1_out,
       nand_2_out, not_1_out, not_2_out;

  Clock clock_1 (.out(clock_1_out));
  D_Flip_Flop d_ff_1 (.clk(clock_1_out), .D(d_ff_1_qn), .Q(out_6), .Qn(d_ff_1_qn));  // open: preset, en, reset
  Clock clock_2 (.out(clock_2_out));
  D_Flip_Flop d_ff_2 (
    .clk(clock_2_out), .D(d_ff_2_qn), .Q(out_2), .Qn(d_ff_2_qn), .reset(nand_1_out));  // open: preset, en
  D_Flip_Flop d_ff_3 (
    .clk(d_ff_2_qn), .D(d_ff_3_qn), .Q(out_3), .Qn(d_ff_3_qn), .reset(nand_1_out));  // open: preset, en
  not not_1 (not_1_out, out_2);
  nand nand_1 (nand_1_out, nand_2_out, CLR_L);
  nand nand_2 (nand_2_out, not_1_out, out_3, not_2_out, out_5);
  D_Flip_Flop d_ff_4 (
    .clk(d_ff_3_qn), .D(d_ff_4_qn), .Q(out_4), .Qn(d_ff_4_qn), .reset(nand_1_out));  // open: preset, en
  not not_2 (not_2_out, out_4);
  D_Flip_Flop d_ff_5 (
    .clk(d_ff_4_qn), .D(d_ff_5_qn), .Q(out_5), .Qn(d_ff_5_qn), .reset(nand_1_out));  // open: preset, en
endmodule

module tmps (
  input  CLR_L,
  output out_2,
  output out_3,
  output out_4,
  output out_5
);

  wire d_ff_1_qn, d_ff_2_qn, d_ff_3_qn, nand_1_out, nand_2_out, not_1_out, undriven, undriven_2;

  Clock clock_1 ();  // open: out
  D_Flip_Flop d_ff_1 (.clk(out_2), .D(undriven_2), .Q(out_3), .Qn(d_ff_1_qn), .reset(nand_1_out));  // open: preset, en
  nand nand_1 (nand_1_out, nand_2_out, CLR_L);
  nand nand_2 (nand_2_out, undriven, out_3, out_4, out_5);
  D_Flip_Flop d_ff_2 (.clk(out_3), .D(d_ff_2_qn), .Q(out_4), .Qn(d_ff_2_qn), .reset(nand_1_out));  // open: preset, en
  D_Flip_Flop d_ff_3 (.clk(out_4), .D(d_ff_3_qn), .Q(out_5), .Qn(d_ff_3_qn), .reset(not_1_out));  // open: preset, en
  not not_1 (not_1_out, nand_1_out);
endmodule
