// Logisim project 实验三_3.circ as structural Verilog: 1 circuit, main circuit main
module main (
  input  in_1,
  input  in_2,
  input  in_3,
  output out_4
);

  wire CP_out, d_ff_1_q, d_ff_2_q, d_ff_3_q, d_ff_4_q, nand_1_out, not_1_out, not_2_out;

  Clock CP (.out(CP_out));
  D_Flip_Flop d_ff_1 (.clk(CP_out), .D(in_1), .Q(d_ff_1_q), .en(in_2));  // open: Qn, preset, reset
  D_Flip_Flop d_ff_2 (.clk(CP_out), .D(d_ff_1_q), .Q(d_ff_2_q), .en(in_3));  // open: Qn, preset, reset
  not not_1 (not_1_out, d_ff_2_q);
  nand nand_1 (nand_1_out, d_ff_1_q, not_1_out, not_2_out, d_ff_4_q);
  D_Flip_Flop d_ff_3 (.clk(CP_out), .D(d_ff_2_q), .Q(d_ff_3_q));  // open: Qn, preset, en, reset
  not not_2 (not_2_out, d_ff_3_q);
  not not_3 (out_4, nand_1_out);
  D_Flip_Flop d_ff_4 (.clk(CP_out), .D(d_ff_3_q), .Q(d_ff_4_q));  // open: Qn, preset, en, reset
endmodule
