// Logisim project 实验三_4.circ as structural Verilog: 2 circuits, main circuit main
module main (
);

  wire and_1_out, and_2_out, clock_1_out, d_ff_1_q, d_ff_2_q, d_ff_3_q, d_ff_4_q, nor_1_out, not_1_out,
       or_1_out, temp_1_x, temp_1_y;

  Clock clock_1 (.out(clock_1_out));
  nor nor_1 (nor_1_out, or_1_out, d_ff_1_q);
  D_Flip_Flop d_ff_1 (.clk(clock_1_out), .D(and_1_out), .Q(d_ff_1_q));  // open: Qn, preset, en, reset
  or or_1 (or_1_out, temp_1_y, temp_1_x);
  D_Flip_Flop d_ff_2 (.clk(clock_1_out), .D(nor_1_out), .Q(d_ff_2_q));  // open: Qn, preset, en, reset
  D_Flip_Flop d_ff_3 (.clk(clock_1_out), .D(d_ff_2_q), .Q(d_ff_3_q));  // open: Qn, preset, en, reset
  D_Flip_Flop d_ff_4 (.clk(clock_1_out), .D(d_ff_3_q), .Q(d_ff_4_q));  // open: Qn, preset, en, reset
  not not_1 (not_1_out, and_2_out);
  temp temp_1 (.a(d_ff_4_q), .b(d_ff_3_q), .c(d_ff_2_q), .d(d_ff_1_q), .x(temp_1_x), .y(temp_1_y));
  and and_1 (and_1_out, d_ff_4_q, not_1_out);
  and and_2 (and_2_out, temp_1_y, temp_1_x);
endmodule

module temp (
  input  a,
  input  b,
  input  c,
  input  d,
  output x,
  output y
);

  wire and_1_out, and_2_out, and_3_out, and_4_out, and_5_out, and_6_out;

  or or_1 (x, d, c, b, a);
  and and_1 (and_1_out, c, d);
  and and_2 (and_2_out, b, d);
  and and_3 (and_3_out, b, c);
  and and_4 (and_4_out, a, d);
  and and_5 (and_5_out, a, c);
  and and_6 (and_6_out, a, b);
  or or_2 (y, and_1_out, and_2_out, and_3_out, and_4_out, and_5_out, and_6_out);
endmodule
