// Logisim project lab2_3_good.circ as structural Verilog: 1 circuit, main circuit main
module main (
  input  in_1,
  input  in_2,
  input  in_3,
  input  in_4,
  output out_5
);

  wire not_1_out, xor_1_out, xor_2_out;

  xor xor_1 (xor_1_out, in_1, in_2);
  xor xor_2 (xor_2_out, xor_1_out, in_3);
  not not_1 (not_1_out, xor_2_out);
  nand nand_1 (out_5, not_1_out, in_4);
endmodule
