// Logisim project lab2_4 - 副本.circ as structural Verilog: 5 circuits, main circuit main
module main (
  input  Z,
  input  Y,
  input  X,
  input  W,
  output out_5
);

  wire n74x138_1_p7, n74x138_1_p8, n74x138_1_p9, n74x138_1_p10, n74x138_2_p7;

  // _74x138 74x138_1: pin names not known; wires that end beside it: 1'b1, W, 1'b0, Z, Y, X, n74x138_1_p7, n74x138_1_p8, n74x138_1_p9, n74x138_1_p10
  // _74x138 74x138_2: pin names not known; wires that end beside it: W, 1'b0, 1'b0, Z, Y, X, n74x138_2_p7, n74x138_2_p7, n74x138_2_p7, n74x138_2_p7
  nand nand_1 (out_5, n74x138_1_p7, n74x138_1_p8, n74x138_1_p9, n74x138_1_p10, n74x138_2_p7);
endmodule

module _74x280 (
  input  in_1,
  input  in_2,
  input  in_3,
  input  in_4,
  input  in_5,
  input  in_6,
  input  in_7,
  input  in_8,
  input  in_9,
  output out_10,
  output out_11
);

  wire not_1_out, xor_1_out, xor_2_out, xor_3_out, xor_4_out, xor_5_out, xor_6_out, xor_7_out, xor_8_out;

  xor xor_1 (xor_1_out, in_1, in_2);
  xor xor_2 (xor_2_out, in_4, in_5);
  xor xor_3 (xor_3_out, in_7, in_8);
  xor xor_4 (xor_4_out, xor_1_out, in_3);
  xor xor_5 (xor_5_out, xor_2_out, in_6);
  xor xor_6 (xor_6_out, xor_3_out, in_9);
  xor xor_7 (xor_7_out, xor_4_out, xor_5_out);
  xor xor_8 (xor_8_out, xor_4_out, xor_5_out);
  not not_1 (not_1_out, xor_6_out);
  xor xor_9 (out_10, xor_7_out, not_1_out);
  xor xor_10 (out_11, xor_8_out, xor_6_out);
endmodule

module _74x138 (
  input  a,
  input  b,
  input  c,
  input  f,
  input  d,
  input  e,
  output x,
  output y,
  output z,
  output u,
  output v,
  output w,
  output s,
  output t
);

  wire nand_1_out, nand_2_out, nand_3_out, nand_4_out, nand_5_out, nand_6_out, nand_7_out, nand_8_out,
       nand_9_out, nand_10_out, nand_11_out, nand_12_out, nand_13_out, nand_14_out, nand_15_out, nand_16_out,
       nand_17_out, nand_18_out, nand_19_out, nand_20_out, nand_21_out, nand_22_out, nand_23_out,
       nand_24_out, nand_25_out, nand_26_out, nand_27_out, nand_28_out;

  nand nand_1 (nand_1_out, c, c);
  nand nand_2 (nand_2_out, b, b);
  nand nand_3 (nand_3_out, e, e);
  nand nand_4 (nand_4_out, c, c);
  nand nand_5 (nand_5_out, b, b);
  nand nand_6 (nand_6_out, d, d);
  nand nand_7 (nand_7_out, c, c);
  nand nand_8 (nand_8_out, b, b);
  nand nand_9 (nand_9_out, e, e);
  nand nand_10 (nand_10_out, d, d);
  nand nand_11 (nand_11_out, c, c);
  nand nand_12 (nand_12_out, b, b);
  nand nand_13 (nand_13_out, f, f);
  nand nand_14 (nand_14_out, c, c);
  nand nand_15 (nand_15_out, b, b);
  nand nand_16 (nand_16_out, e, e);
  nand nand_17 (nand_17_out, f, f);
  nand nand_18 (nand_18_out, c, c);
  nand nand_19 (nand_19_out, b, b);
  nand nand_20 (nand_20_out, d, d);
  nand nand_21 (nand_21_out, f, f);
  nand nand_22 (nand_22_out, c, c);
  nand nand_23 (nand_23_out, b, b);
  nand nand_24 (nand_24_out, e, e);
  nand nand_25 (nand_25_out, d, d);
  nand nand_26 (nand_26_out, f, f);
  nand nand_27 (nand_27_out, c, c);
  nand nand_28 (nand_28_out, b, b);
  nand nand_29 (x, a, f, d, e, nand_1_out, nand_2_out);
  nand nand_30 (y, a, f, d, nand_3_out, nand_4_out, nand_5_out);
  nand nand_31 (z, a, f, e, nand_6_out, nand_7_out, nand_8_out);
  nand nand_32 (u, a, f, nand_9_out, nand_10_out, nand_11_out, nand_12_out);
  nand nand_33 (v, a, d, e, nand_13_out, nand_14_out, nand_15_out);
  nand nand_34 (w, a, d, nand_16_out, nand_17_out, nand_18_out, nand_19_out);
  nand nand_35 (s, a, e, nand_20_out, nand_21_out, nand_22_out, nand_23_out);
  nand nand_36 (t, a, nand_24_out, nand_25_out, nand_26_out, nand_27_out, nand_28_out);
endmodule

module t (
  input  in_1,
  input  in_2,
  input  in_3,
  input  in_4,
  input  in_5,
  input  in_6,
  output F,
  output G
);

  wire n74x138_1_s, n74x138_1_z, n74x138_2_u, n74x138_2_x, n74x138_2_z;

  _74x138 u_74x138_1 (
    .a(1'b1), .b(1'b0), .c(1'b0), .f(in_1), .d(in_2), .e(in_3), .z(n74x138_1_z), .s(n74x138_1_s));  // open: x, y, u, v, w, t
  _74x138 u_74x138_2 (
    .a(1'b1), .x(n74x138_2_x), .b(1'b0), .c(1'b0), .f(in_4), .d(in_5), .e(in_6), .z(n74x138_2_z),
    .u(n74x138_2_u));  // open: y, v, w, s, t
  nand nand_1 (F, n74x138_1_z, n74x138_1_s);
  nand nand_2 (G, n74x138_2_x, n74x138_2_z, n74x138_2_u);
endmodule

module _6_50 (
  input  in_1,
  input  in_2,
  input  in_3,
  input  in_4,
  input  in_5,
  input  in_6,
  input  in_7,
  input  in_8,
  input  in_9,
  input  in_10,
  output out_11,
  output C,
  output B,
  output A
);

  or or_1 (out_11, in_2, in_4, in_6, in_6);
  or or_2 (C, in_3, in_4, in_7, in_6, in_6);
  or or_3 (B, in_7, in_6, in_5, in_6, in_6);
  or or_4 (A, in_6, in_6);

  assign in_8 = in_6;
  assign in_9 = in_6;
  assign in_10 = in_6;
endmodule
