// Logisim project lab2_4.circ as structural Verilog: 3 circuits, main circuit main
module main (
  input  in_1,
  input  in_2,
  input  in_3,
  input  in_4,
  input  in_5,
  input  in_6,
  input  in_7,
  input  in_8,
  input  in_9,
  input  in_10,
  input  in_11,
  input  in_12,
  input  in_13,
  input  in_14,
  input  in_15,
  input  in_16,
  input  in_17,
  input  in_18,
  input  in_19,
  output out_20,
  output out_21,
  output out_22,
  output out_23,
  output out_24,
  output out_25,
  output out_26,
  output out_27
);

  wire n74x138_1_s, n74x138_1_u, n74x138_1_v, n74x138_1_w, n74x138_1_x, n74x138_1_y, n74x138_1_z,
       n74x280_1_out_11, n74x280_2_out_11, n74x280_3_out_11, xor_1_out, xor_2_out, xor_3_out, xor_4_out,
       xor_5_out, xor_6_out, xor_7_out;

  _74x280 u_74x280_1 (
    .in_1(in_1), .in_2(in_2), .in_3(in_3), .in_4(in_4), .in_5(1'b0), .in_6(1'b0), .in_7(1'b0), .in_8(1'b0),
    .in_9(1'b0), .out_11(n74x280_1_out_11));  // open: out_10
  _74x280 u_74x280_2 (
    .in_1(in_7), .in_2(in_8), .in_3(in_10), .in_4(in_11), .in_5(1'b0), .in_6(1'b0), .in_7(1'b0), .in_8(1'b0),
    .in_9(1'b0), .out_11(n74x280_2_out_11));  // open: out_10
  _74x280 u_74x280_3 (
    .in_1(in_15), .in_2(in_16), .in_3(in_18), .in_4(in_19), .in_5(1'b0), .in_6(1'b0), .in_7(1'b0),
    .in_8(1'b0), .in_9(1'b0), .out_11(n74x280_3_out_11));  // open: out_10
  _74x138 u_74x138_1 (
    .a(1'b1), .x(n74x138_1_x), .b(1'b0), .c(1'b0), .f(n74x280_3_out_11), .y(n74x138_1_y),
    .d(n74x280_2_out_11), .e(n74x280_1_out_11), .z(n74x138_1_z), .u(n74x138_1_u), .v(n74x138_1_v),
    .w(n74x138_1_w), .s(n74x138_1_s), .t(out_27));
  xor xor_1 (xor_1_out, in_5, n74x138_1_s);
  xor xor_2 (xor_2_out, in_6, n74x138_1_w);
  xor xor_3 (xor_3_out, in_9, n74x138_1_v);
  xor xor_4 (xor_4_out, in_12, n74x138_1_u);
  xor xor_5 (xor_5_out, in_13, n74x138_1_z);
  xor xor_6 (xor_6_out, in_14, n74x138_1_y);
  xor xor_7 (xor_7_out, in_17, n74x138_1_x);
  not not_1 (out_20, xor_1_out);
  not not_2 (out_21, xor_2_out);
  not not_3 (out_22, xor_3_out);
  not not_4 (out_23, xor_4_out);
  not not_5 (out_24, xor_5_out);
  not not_6 (out_25, xor_6_out);
  not not_7 (out_26, xor_7_out);
endmodule

module _74x280 (
  input  in_1,
  input  in_2,
  input  in_3,
  input  in_4,
  input  in_5,
  input  in_6,
  input  in_7,
  input  in_8,
  input  in_9,
  output out_10,
  output out_11
);

  wire not_1_out, xor_1_out, xor_2_out, xor_3_out, xor_4_out, xor_5_out, xor_6_out, xor_7_out, xor_8_out;

  xor xor_1 (xor_1_out, in_1, in_2);
  xor xor_2 (xor_2_out, in_4, in_5);
  xor xor_3 (xor_3_out, in_7, in_8);
  xor xor_4 (xor_4_out, xor_1_out, in_3);
  xor xor_5 (xor_5_out, xor_2_out, in_6);
  xor xor_6 (xor_6_out, xor_3_out, in_9);
  xor xor_7 (xor_7_out, xor_4_out, xor_5_out);
  xor xor_8 (xor_8_out, xor_4_out, xor_5_out);
  not not_1 (not_1_out, xor_6_out);
  xor xor_9 (out_10, xor_7_out, not_1_out);
  xor xor_10 (out_11, xor_8_out, xor_6_out);
endmodule

module _74x138 (
  input  a,
  input  b,
  input  c,
  input  f,
  input  d,
  input  e,
  output x,
  output y,
  output z,
  output u,
  output v,
  output w,
  output s,
  output t
);

  wire nand_1_out, nand_2_out, nand_3_out, nand_4_out, nand_5_out, nand_6_out, nand_7_out, nand_8_out,
       nand_9_out, nand_10_out, nand_11_out, nand_12_out, nand_13_out, nand_14_out, nand_15_out, nand_16_out,
       nand_17_out, nand_18_out, nand_19_out, nand_20_out, nand_21_out, nand_22_out, nand_23_out,
       nand_24_out, nand_25_out, nand_26_out, nand_27_out, nand_28_out;

  nand nand_1 (nand_1_out, c, c);
  nand nand_2 (nand_2_out, b, b);
  nand nand_3 (nand_3_out, e, e);
  nand nand_4 (nand_4_out, c, c);
  nand nand_5 (nand_5_out, b, b);
  nand nand_6 (nand_6_out, d, d);
  nand nand_7 (nand_7_out, c, c);
  nand nand_8 (nand_8_out, b, b);
  nand nand_9 (nand_9_out, e, e);
  nand nand_10 (nand_10_out, d, d);
  nand nand_11 (nand_11_out, c, c);
  nand nand_12 (nand_12_out, b, b);
  nand nand_13 (nand_13_out, f, f);
  nand nand_14 (nand_14_out, c, c);
  nand nand_15 (nand_15_out, b, b);
  nand nand_16 (nand_16_out, e, e);
  nand nand_17 (nand_17_out, f, f);
  nand nand_18 (nand_18_out, c, c);
  nand nand_19 (nand_19_out, b, b);
  nand nand_20 (nand_20_out, d, d);
  nand nand_21 (nand_21_out, f, f);
  nand nand_22 (nand_22_out, c, c);
  nand nand_23 (nand_23_out, b, b);
  nand nand_24 (nand_24_out, e, e);
  nand nand_25 (nand_25_out, d, d);
  nand nand_26 (nand_26_out, f, f);
  nand nand_27 (nand_27_out, c, c);
  nand nand_28 (nand_28_out, b, b);
  nand nand_29 (x, a, f, d, e, nand_1_out, nand_2_out);
  nand nand_30 (y, a, f, d, nand_3_out, nand_4_out, nand_5_out);
  nand nand_31 (z, a, f, e, nand_6_out, nand_7_out, nand_8_out);
  nand nand_32 (u, a, f, nand_9_out, nand_10_out, nand_11_out, nand_12_out);
  nand nand_33 (v, a, d, e, nand_13_out, nand_14_out, nand_15_out);
  nand nand_34 (w, a, d, nand_16_out, nand_17_out, nand_18_out, nand_19_out);
  nand nand_35 (s, a, e, nand_20_out, nand_21_out, nand_22_out, nand_23_out);
  nand nand_36 (t, a, nand_24_out, nand_25_out, nand_26_out, nand_27_out, nand_28_out);
endmodule
