// Logisim project lab2_addition.circ as structural Verilog: 1 circuit, main circuit main
module main (
  input  X,
  input  Y,
  input  CIN,
  output S,
  output COUT
);

  wire and_1_out, and_2_out, and_3_out, xor_1_out;

  xor xor_1 (xor_1_out, X, Y);
  and and_1 (and_1_out, CIN, X);
  and and_2 (and_2_out, CIN, Y);
  and and_3 (and_3_out, Y, X);
  xor xor_2 (S, xor_1_out, CIN);
  or or_1 (COUT, and_1_out, and_2_out, and_3_out);
endmodule
