// Logisim project lab2_1.circ as structural Verilog: 1 circuit, main circuit main
module main (
  input  A,
  input  B,
  input  CI,
  output S,
  output _6
);

  wire HC00_2_out, HC00_out, HC02_out, HC86_out, not_1_out, not_2_out;

  xor HC86 (HC86_out, A, B);
  nand HC00 (HC00_out, A, B);
  not not_1 (not_1_out, HC00_out);
  xor HC86_2 (S, HC86_out, CI);
  nand HC00_2 (HC00_2_out, HC86_out, CI);
  not not_2 (not_2_out, HC00_2_out);
  nor HC02 (HC02_out, not_2_out, not_1_out);
  not not_3 (_6, HC02_out);

  // Notes on the sheet:
  //   1
  //   2
  //   1
  //   2
  //   1
  //   HC04
  //   3
  //   2
  //   4
  //   5
  //   5
  //   4
  //   6
  //   6
  //   HC04
  //   3
  //   4
  //   11
  //   12
  //   5
  //   13
  //   HC04
endmodule
