// Logisim project lab2_5.circ as structural Verilog: 2 circuits, main circuit main
module main (
  input  A,
  input  B,
  input  x1,
  input  x2,
  input  x3,
  output y1,
  output y2,
  output y3
);

  wire and_1_out, and_2_out, and_3_out, and_4_out, and_5_out, and_6_out, and_7_out, and_8_out, not_1_out,
       not_2_out, not_3_out, not_4_out, not_5_out, not_6_out, not_7_out, not_8_out, not_9_out, not_10_out,
       not_11_out;

  not not_1 (not_1_out, A);
  not not_2 (not_2_out, B);
  not not_3 (not_3_out, A);
  not not_4 (not_4_out, x2);
  not not_5 (not_5_out, x2);
  not not_6 (not_6_out, x3);
  not not_7 (not_7_out, A);
  not not_8 (not_8_out, x1);
  not not_9 (not_9_out, x3);
  not not_10 (not_10_out, x1);
  not not_11 (not_11_out, x2);
  and and_1 (and_1_out, not_1_out, not_2_out, x1);
  and and_2 (and_2_out, not_3_out, x1, not_4_out);
  and and_3 (and_3_out, x1, not_5_out, not_6_out);
  and and_4 (and_4_out, not_7_out, not_8_out, x2);
  and and_5 (and_5_out, B, x2);
  and and_6 (and_6_out, A, x2, not_9_out);
  and and_7 (and_7_out, not_10_out, not_11_out, x3);
  and and_8 (and_8_out, A, x3);
  or or_1 (y1, and_1_out, and_2_out, and_3_out);
  or or_2 (y2, and_4_out, and_5_out, and_6_out);
  or or_3 (y3, and_7_out, and_8_out);
endmodule

module main1 (
  input  A,
  input  B,
  input  x1,
  input  x2,
  input  x3,
  output y1,
  output y2,
  output y3
);

  wire not_1_out, not_2_out, not_3_out, not_4_out, not_5_out, not_6_out, not_7_out, not_8_out, not_9_out,
       not_10_out, not_11_out, or_1_out, or_2_out, or_3_out, or_4_out, or_5_out, or_6_out, or_7_out;

  not not_1 (not_1_out, B);
  not not_2 (not_2_out, x2);
  not not_3 (not_3_out, A);
  not not_4 (not_4_out, x3);
  not not_5 (not_5_out, A);
  not not_6 (not_6_out, x2);
  not not_7 (not_7_out, x1);
  not not_8 (not_8_out, A);
  not not_9 (not_9_out, x3);
  not not_10 (not_10_out, x2);
  not not_11 (not_11_out, x1);
  or or_1 (or_1_out, not_1_out, not_2_out);
  or or_2 (or_2_out, not_3_out, not_4_out);
  or or_3 (or_3_out, not_5_out, not_6_out);
  or or_4 (or_4_out, A, B, not_7_out);
  or or_5 (or_5_out, not_8_out, B, not_9_out);
  or or_6 (or_6_out, A, not_10_out);
  or or_7 (or_7_out, A, not_11_out);
  and and_1 (y1, x1, or_1_out, or_2_out, or_3_out);
  and and_2 (y2, x2, or_4_out, or_5_out);
  and and_3 (y3, x3, or_6_out, or_7_out);
endmodule
