// Logisim project lab2_5_advance.circ as structural Verilog: 5 circuits, main circuit main
module main (
  input  A,
  input  B,
  input  x1,
  input  x2,
  input  x3,
  output y1,
  output y2,
  output y3
);

  wire and_1_out, and_2_out, and_3_out, and_4_out, and_5_out, and_6_out, and_7_out, and_8_out, not_1_out,
       not_2_out, not_3_out, not_4_out, not_5_out, not_6_out, not_7_out, not_8_out, not_9_out, not_10_out,
       not_11_out;

  not not_1 (not_1_out, A);
  not not_2 (not_2_out, B);
  not not_3 (not_3_out, A);
  not not_4 (not_4_out, x2);
  not not_5 (not_5_out, x2);
  not not_6 (not_6_out, x3);
  not not_7 (not_7_out, A);
  not not_8 (not_8_out, x1);
  not not_9 (not_9_out, x3);
  not not_10 (not_10_out, x1);
  not not_11 (not_11_out, x2);
  and and_1 (and_1_out, not_1_out, not_2_out, x1);
  and and_2 (and_2_out, not_3_out, x1, not_4_out);
  and and_3 (and_3_out, x1, not_5_out, not_6_out);
  and and_4 (and_4_out, not_7_out, not_8_out, x2);
  and and_5 (and_5_out, B, x2);
  and and_6 (and_6_out, A, x2, not_9_out);
  and and_7 (and_7_out, not_10_out, not_11_out, x3);
  and and_8 (and_8_out, A, x3);
  or or_1 (y1, and_1_out, and_2_out, and_3_out);
  or or_2 (y2, and_4_out, and_5_out, and_6_out);
  or or_3 (y3, and_7_out, and_8_out);
endmodule

module advance (
  input  x1,
  input  x2,
  input  x3,
  output y1,
  output y2,
  output y3
);

  wire not_1_out, not_2_out, not_3_out;

  not not_1 (not_1_out, x1);
  not not_2 (not_2_out, x1);
  not not_3 (not_3_out, x2);
  and and_1 (y2, not_1_out, x2);
  and and_2 (y3, not_2_out, not_3_out, x3);

  assign y1 = x1;
endmodule

module advance1 (
  input  x1,
  input  x2,
  input  x3,
  output y1,
  output y2,
  output y3
);

  wire not_1_out, not_2_out, not_3_out;

  not not_1 (not_1_out, x2);
  not not_2 (not_2_out, x1);
  not not_3 (not_3_out, x2);
  and and_1 (y1, x1, not_1_out);
  and and_2 (y3, not_2_out, not_3_out, x3);

  assign y2 = x2;
endmodule

module advance2 (
  input  x1,
  input  x2,
  input  x3,
  output y1,
  output y2,
  output y3
);

  wire not_1_out, not_2_out, not_3_out;

  not not_1 (not_1_out, x2);
  not not_2 (not_2_out, x3);
  not not_3 (not_3_out, x3);
  and and_1 (y1, x1, not_1_out, not_2_out);
  and and_2 (y2, x2, not_3_out);

  assign y3 = x3;
endmodule

module additionAll (
  input  in_1,
  input  in_2,
  input  in_3
);
endmodule
